# Fritzing sketch midi-octopot (saved by Fritzing 0.9.6b)
breadboards: 1

parts:
  R1 = Rotary Potentiometer (Large) [maximum_resistance=10kΩ package=THT]
  R2 = Rotary Potentiometer (Large) [maximum_resistance=10kΩ package=THT]
  R3 = Rotary Potentiometer (Large) [maximum_resistance=10kΩ package=THT]
  R4 = Rotary Potentiometer (Large) [maximum_resistance=10kΩ package=THT]
  R5 = Rotary Potentiometer (Large) [maximum_resistance=10kΩ package=THT]
  R6 = Rotary Potentiometer (Large) [maximum_resistance=10kΩ package=THT]
  R7 = Rotary Potentiometer (Large) [maximum_resistance=10kΩ package=THT]
  R8 = Rotary Potentiometer (Large) [maximum_resistance=10kΩ package=THT]
  Microcontroller = Arduino Micro (Rev3)

nets:
  GND: R1.leg1, R2.leg1, R3.leg1, R4.leg1, R5.leg2, R6.leg2, R7.leg2, R8.leg2, Microcontroller.GND
  N1: R1.wiper, Microcontroller.A0
  5V: R1.leg2, R2.leg2, R3.leg2, R4.leg2, R5.leg1, R6.leg1, R7.leg1, R8.leg1, Microcontroller.5V
  N2: R2.wiper, Microcontroller.A1
  N3: R3.wiper, Microcontroller.A2
  N4: R4.wiper, Microcontroller.A3
  N5: R5.wiper, Microcontroller.D10_PWM/A10
  N6: R6.wiper, Microcontroller.D9_PWM/A9
  N7: R7.wiper, Microcontroller.D7
  N8: R8.wiper, Microcontroller.D6_PWM/A7

// code stored in the sketch: midi-octopot.ino
#include <MIDIUSB.h>
#include <MIDIUSB_Defs.h>

enum {
    MIDI_CC_PORTAMENTO_TIME             = 0x05,
    MIDI_CC_VOLUME                      = 0x07,
    MIDI_CC_PAN_MSB                     = 0x0A,

    MIDI_CC_SOUND_CONTROLLER_2          = 0x47, // Timbre/Harmonic Intensity
    MIDI_CC_SOUND_CONTROLLER_3          = 0x48, // Release Time
    MIDI_CC_SOUND_CONTROLLER_4          = 0x49, // Attack Time
    MIDI_CC_SOUND_CONTROLLER_5          = 0x4A, // Brightness
    MIDI_CC_EFFECTS_1_DEPTH             = 0x5B, // Reverb amount
    MIDI_CC_EFFECTS_4_DEPTH             = 0x5F, // Detune amount
};

#define MIDI_CHANNEL 0
#define POT_NB 8

byte pot_pin[] = {A0,  A1, A2, A3,
                  A10, A9, A8, A7};

byte pot_mcc[] = {MIDI_CC_SOUND_CONTROLLER_2, MIDI_CC_SOUND_CONTROLLER_3, MIDI_CC_PORTAMENTO_TIME, MIDI_CC_EFFECTS_1_DEPTH, 
                  MIDI_CC_SOUND_CONTROLLER_5, MIDI_CC_SOUND_CONTROLLER_4, MIDI_CC_EFFECTS_4_DEPTH, MIDI_CC_PAN_MSB};

byte pot_val[] = {0, 0, 0, 0, 0, 0, 0, 0};

void controlChange(byte channel, byte control, byte value) {

  midiEventPacket_t event = {0x0B, 0xB0 | channel, control, value};

  MidiUSB.sendMIDI(event);
  MidiUSB.flush();
}

void setup() {
  // put your setup code here, to run once:
   Serial.begin(115200);
}

void loop() {
  // put your main code here, to run repeatedly:
  for (byte i = 0; i < POT_NB; i++)
  {
    byte val = analogRead(pot_pin[i]) / 8;
    if (val != pot_val[i])
    {
      pot_val[i] = val;
      controlChange(MIDI_CHANNEL, pot_mcc[i], pot_val[i]);
    }
    char buf[5];
    sprintf(buf, "%3d ", (int)pot_val[i]);
    Serial.print(buf);
  }
  Serial.println();
}
